# Fritzing sketch Schematic (saved by Fritzing 0.9.2b)
breadboards: 1

parts:
  Part1 = Arduino Nano (Rev3.0)
  Molex_Power_Connector = COMPUTER-PERIPHERAL-POWER [package=computer-peripheral-power-ra]
  RGB_LED_Strip = ws2812b [package="smd 2812b"]

nets:
  N1: Part1.D5, RGB_LED_Strip.DIN
  VIN: Part1.VIN, Molex_Power_Connector.GND, RGB_LED_Strip.VSS
  5V: Part1.5V, Molex_Power_Connector.5V, RGB_LED_Strip.VDD
